# Fritzing sketch fritzing-project-design (saved by Fritzing 0.9.3b)
breadboards: 2

parts:
  Part1 = Arduino Uno (Rev3) - ICSP
  R1 = Resistor [tolerance=±5% resistance=10k package=THT]
  R3 = Resistor [tolerance=±5% resistance=10k package=THT]
  R4 = Resistor [tolerance=±5% resistance=10k package=THT]
  R5 = Resistor [tolerance=±5% resistance=10k package=THT]
  Part3 = SRF05 Ultrasonic Rangefinder
  Part4 = Arduino Uno (Rev3) - ICSP
  부품3 = FC-28 Soil Hygrometer Module
  부품4 = FC-28 Soil Hygrometer Module - Probe
  VALVE2 = Plastic Solenoid Valve
  VALVE3 = Plastic Solenoid Valve
  VALVE4 = Plastic Solenoid Valve
  MCU1 = Raspberry Pi Zero
  LCD2 = LCD screen
  LCM1602_IIC2 = LCM1602 IIC [part_number="LCM1602 IIC" chip_label="LCM1602 IIC" package="DIP (Dual Inline) [THT]"]
  Part6 = I2C level shifter bidirectional
  KY-1 = Keyes Relay [package=THT]
  LED1 = smd LED [color="Red (633nm)" package="0805 [SMD]"]
  LED2 = smd LED [color="Green (555nm)" package="0805 [SMD]"]

nets:
  N1: Part1.A0, R1.Pin_0
  N2: Part1.A1, R3.Pin_0
  N3: Part1.A2, R4.Pin_0
  N4: Part1.A3, R5.Pin_0
  N5: Part1.A4/SDA, Part4.A4/SDA, Part6.HV2
  5V: Part1.5V, Part3.VCC, Part6.HV
  GND: Part1.GND, R1.Pin_1, R3.Pin_1, R4.Pin_1, R5.Pin_1, Part3.GND, MCU1.pin_6, MCU1.pin_9, MCU1.pin_39, LCM1602_IIC2.GND, Part6.GND, KY-1.ground, LED1.cathode, LED2.cathode
  N6: Part1.A5/SCL, Part4.A5/SCL, Part6.HV1
  N7: Part1.D3_PWM, Part3.Echo
  N8: Part1.D4, Part3.Trig
  N9: Part4.A0, 부품3.AO
  N10: Part4.D4, VALVE2.no_name_yet#2
  N11: Part4.D5_PWM, VALVE4.no_name_yet#2
  N12: Part4.D6_PWM, VALVE3.no_name_yet#2
  5V_2: Part4.5V, 부품3.VCC
  GND_2: Part4.GND, 부품3.GND, VALVE2.no_name_yet#1, VALVE3.no_name_yet#1, VALVE4.no_name_yet#1
  N13: 부품3.POS, 부품4.POS
  N14: 부품3.NEG, 부품4.NEG
  N15: MCU1.pin_2, LCM1602_IIC2.VCC, Part6.LV, KY-1.power
  N16: MCU1.pin_3, LCM1602_IIC2.SDA, Part6.LV2
  N17: MCU1.pin_5, LCM1602_IIC2.SCL, Part6.LV1
  N18: MCU1.pin_7, KY-1.signal
  N19: MCU1.pin_29, LED1.anode
  N20: MCU1.pin_33, LED2.anode
  VSS: LCD2.VSS, LCM1602_IIC2.VSS
  VDD: LCD2.VDD, LCM1602_IIC2.VDD
  N21: LCD2.V0, LCM1602_IIC2.V0
  N22: LCD2.RS, LCM1602_IIC2.RS
  N23: LCD2.R/W, LCM1602_IIC2.RW
  N24: LCD2.E, LCM1602_IIC2.E
  N25: LCD2.DB0, LCM1602_IIC2.D0
  N26: LCD2.DB1, LCM1602_IIC2.D1
  N27: LCD2.DB2, LCM1602_IIC2.D2
  N28: LCD2.DB3, LCM1602_IIC2.D3
  N29: LCD2.DB4, LCM1602_IIC2.D4
  N30: LCD2.DB5, LCM1602_IIC2.D5
  N31: LCD2.DB6, LCM1602_IIC2.D6
  N32: LCD2.DB7, LCM1602_IIC2.D7
  N33: LCD2.LED+, LCM1602_IIC2.A
  N34: LCD2.LED-, LCM1602_IIC2.K
  N35: LCM1602_IIC2.LED_A, LCM1602_IIC2.LED_B

notes:
  Level 1
  Level 3
  Level 2
  Level 4

custom parts:
  FC-28 Soil Hygrometer Module: The FC-28 is a soil hygrometer module that uses the Texas Instruments LM393 comparator chip to provide an analog measurement of soil humidity. The digital output is high when soil moisture is over a certain threshold, as determined by adjusting the potentiometer.
  FC-28 Soil Hygrometer Module - Probe: The FC-28 is a soil hygrometer module that uses the Texas Instruments LM393 comparator chip to provide an analog measurement of soil humidity.
  LCM1602 IIC: I2C-Module to use a 1602 or 2004 LCD on with the wire.h libory Serial LCD Modul
  Keyes Relay: The Keyes 5V relay module is suitable for SCM development, home appliance control. It uses a 5V~12V TIL control signal which can control DC / AC signal.
